// Logisim project CPU.circ as structural Verilog: 7 circuits, main circuit CPU
module CPU (
  input  enabler,
  input  Reset,
  input  Interrupt,
  input  HaltRun
);

  wire clock_1_out;
  wire [15:0] InstructionStorage_data, pc_1_o;

  Clock clock_1 (.out(clock_1_out));
  PC pc_1 (.jump_e(enabler), .clock(clock_1_out), .O(pc_1_o));  // open: jump_addr, reset
  ROM #(.addrWidth(16), .dataWidth(16)) InstructionStorage (.addr(pc_1_o), .data(InstructionStorage_data));
  Register #(.width(16)) InstructionRegister (.D(InstructionStorage_data));  // open: en, clk, Q, clr
  RegFile regfile_1 (.clock(clock_1_out));  // open: readRegister1, readRegister2, writeReg, writeData, regWriteEnabler, read_a, read_b

  // Notes on the sheet:
  //   contents of InstructionStorage (hex, n*v repeats v):
  //   1234 abcd 5678
endmodule

module PC (
  input  [15:0] jump_addr,
  input  jump_e,
  input  clock,
  input  reset,
  output [15:0] O
);

  wire [15:0] multiplexer_1_out, sixteenbitadder_1_o;

  sixteenbitadder sixteenbitadder_1 (.Cin(1'b1), .A(O), .O(sixteenbitadder_1_o));  // open: B, Cout
  Multiplexer #(.width(16)) multiplexer_1 (
    .in0(sixteenbitadder_1_o), .in1(jump_addr), .out(multiplexer_1_out), .sel(jump_e));
  Register #(.width(16)) register_1 (.D(multiplexer_1_out), .en(1'b1), .clk(clock), .Q(O), .clr(reset));
endmodule

module sixteenbitadder (
  input  Cin,
  input  [15:0] A,
  input  [15:0] B,
  output [15:0] O,
  output Cout
);

  wire fourbitadder_1_cout, fourbitadder_2_cout, fourbitadder_3_cout;

  fourbitadder fourbitadder_1 (.Cin(Cin), .A(A[3:0]), .B(B[3:0]), .O(O[3:0]), .Cout(fourbitadder_1_cout));
  fourbitadder fourbitadder_2 (
    .Cin(fourbitadder_1_cout), .A(A[7:4]), .B(B[7:4]), .O(O[7:4]), .Cout(fourbitadder_2_cout));
  fourbitadder fourbitadder_3 (
    .Cin(fourbitadder_2_cout), .A(A[11:8]), .B(B[11:8]), .O(O[11:8]), .Cout(fourbitadder_3_cout));
  fourbitadder fourbitadder_4 (.Cin(fourbitadder_3_cout), .A(A[15:12]), .B(B[15:12]), .O(O[15:12]), .Cout(Cout));
endmodule

module fourbitadder (
  input  Cin,
  input  [3:0] A,
  input  [3:0] B,
  output [3:0] O,
  output Cout
);

  wire fulladder_1_cout, fulladder_2_cout, fulladder_3_cout;

  fulladder fulladder_1 (.Cin(Cin), .A(A[0]), .B(B[0]), .O(O[0]), .Cout(fulladder_1_cout));
  fulladder fulladder_2 (.Cin(fulladder_1_cout), .A(A[1]), .B(B[1]), .O(O[1]), .Cout(fulladder_2_cout));
  fulladder fulladder_3 (.Cin(fulladder_2_cout), .A(A[2]), .B(B[2]), .O(O[2]), .Cout(fulladder_3_cout));
  fulladder fulladder_4 (.Cin(fulladder_3_cout), .A(A[3]), .B(B[3]), .O(O[3]), .Cout(Cout));
endmodule

module halfadder (
  input  A,
  input  B,
  output O,
  output Cout
);

  xor xor_1 (O, A, B);
  and and_1 (Cout, A, B);
endmodule

module fulladder (
  input  Cin,
  input  A,
  input  B,
  output O,
  output Cout
);

  wire halfadder_1_cout, halfadder_2_cout, halfadder_2_o;

  halfadder halfadder_1 (.A(Cin), .B(halfadder_2_o), .O(O), .Cout(halfadder_1_cout));
  halfadder halfadder_2 (.A(A), .B(B), .O(halfadder_2_o), .Cout(halfadder_2_cout));
  or or_1 (Cout, halfadder_1_cout, halfadder_2_cout);
endmodule

module RegFile (
  input  [3:0] readRegister1,
  input  [3:0] readRegister2,
  input  [3:0] writeReg,
  input  [15:0] writeData,
  input  regWriteEnabler,
  input  clock,
  output [15:0] read_a,
  output [15:0] read_b
);

  wire decoder_1_out0, decoder_1_out1, decoder_1_out2, decoder_1_out3, decoder_1_out4, decoder_1_out5,
       decoder_1_out6, decoder_1_out7, decoder_1_out8, decoder_1_out9, decoder_1_out10, decoder_1_out11,
       decoder_1_out12, decoder_1_out13, decoder_1_out14, decoder_1_out15, decoder_2_out0, decoder_2_out1,
       decoder_2_out2, decoder_2_out3, decoder_2_out4, decoder_2_out5, decoder_2_out6, decoder_2_out7,
       decoder_2_out8, decoder_2_out9, decoder_2_out10, decoder_2_out11, decoder_2_out12, decoder_2_out13,
       decoder_2_out14, decoder_2_out15, decoder_3_out0, decoder_3_out1, decoder_3_out2, decoder_3_out3,
       decoder_3_out4, decoder_3_out5, decoder_3_out6, decoder_3_out7, decoder_3_out8, decoder_3_out9,
       decoder_3_out10, decoder_3_out11, decoder_3_out12, decoder_3_out13, decoder_3_out14, decoder_3_out15;
  wire [15:0] reg0_q, reg1_q, reg2_q, reg3_q, reg4_q, reg5_q, reg6_q, reg7_q, reg8_q, reg9_q, reg10_q,
       reg11_q, reg12_q, reg13_q, reg15_q, rqg14_q;

  Decoder #(.enable("false"), .select(4)) decoder_1 (
    .out0(decoder_1_out0), .out1(decoder_1_out1), .out2(decoder_1_out2), .out3(decoder_1_out3),
    .out4(decoder_1_out4), .out5(decoder_1_out5), .out6(decoder_1_out6), .out7(decoder_1_out7),
    .out8(decoder_1_out8), .out9(decoder_1_out9), .out10(decoder_1_out10), .out11(decoder_1_out11),
    .out12(decoder_1_out12), .out13(decoder_1_out13), .out14(decoder_1_out14), .out15(decoder_1_out15),
    .sel(readRegister1));
  Decoder #(.enable("false"), .select(4)) decoder_2 (
    .out0(decoder_2_out0), .out1(decoder_2_out1), .out2(decoder_2_out2), .out3(decoder_2_out3),
    .out4(decoder_2_out4), .out5(decoder_2_out5), .out6(decoder_2_out6), .out7(decoder_2_out7),
    .out8(decoder_2_out8), .out9(decoder_2_out9), .out10(decoder_2_out10), .out11(decoder_2_out11),
    .out12(decoder_2_out12), .out13(decoder_2_out13), .out14(decoder_2_out14), .out15(decoder_2_out15),
    .sel(readRegister2));
  Decoder #(.select(4)) decoder_3 (
    .out0(decoder_3_out0), .out1(decoder_3_out1), .out2(decoder_3_out2), .out3(decoder_3_out3),
    .out4(decoder_3_out4), .out5(decoder_3_out5), .out6(decoder_3_out6), .out7(decoder_3_out7),
    .out8(decoder_3_out8), .out9(decoder_3_out9), .out10(decoder_3_out10), .out11(decoder_3_out11),
    .out12(decoder_3_out12), .out13(decoder_3_out13), .out14(decoder_3_out14), .out15(decoder_3_out15),
    .sel(writeReg), .en(regWriteEnabler));
  Register #(.width(16)) reg0 (.D(writeData), .en(decoder_3_out0), .clk(clock), .Q(reg0_q));  // open: clr
  Register #(.width(16)) reg1 (.D(writeData), .en(decoder_3_out1), .clk(clock), .Q(reg1_q));  // open: clr
  Register #(.width(16)) reg2 (.D(writeData), .en(decoder_3_out2), .clk(clock), .Q(reg2_q));  // open: clr
  Register #(.width(16)) reg3 (.D(writeData), .en(decoder_3_out3), .clk(clock), .Q(reg3_q));  // open: clr
  Register #(.width(16)) reg4 (.D(writeData), .en(decoder_3_out4), .clk(clock), .Q(reg4_q));  // open: clr
  Register #(.width(16)) reg5 (.D(writeData), .en(decoder_3_out5), .clk(clock), .Q(reg5_q));  // open: clr
  Register #(.width(16)) reg6 (.D(writeData), .en(decoder_3_out6), .clk(clock), .Q(reg6_q));  // open: clr
  Register #(.width(16)) reg7 (.D(writeData), .en(decoder_3_out7), .clk(clock), .Q(reg7_q));  // open: clr
  assign read_b = decoder_2_out0 ? reg0_q : 16'bz;  // Controlled_Buffer controlled_buffer_1
  Register #(.width(16)) reg8 (.D(writeData), .en(decoder_3_out8), .clk(clock), .Q(reg8_q));  // open: clr
  Register #(.width(16)) reg9 (.D(writeData), .en(decoder_3_out9), .clk(clock), .Q(reg9_q));  // open: clr
  Register #(.width(16)) reg10 (.D(writeData), .en(decoder_3_out10), .clk(clock), .Q(reg10_q));  // open: clr
  Register #(.width(16)) reg11 (.D(writeData), .en(decoder_3_out11), .clk(clock), .Q(reg11_q));  // open: clr
  Register #(.width(16)) reg12 (.D(writeData), .en(decoder_3_out12), .clk(clock), .Q(reg12_q));  // open: clr
  Register #(.width(16)) reg13 (.D(writeData), .en(decoder_3_out13), .clk(clock), .Q(reg13_q));  // open: clr
  Register #(.width(16)) rqg14 (.D(writeData), .en(decoder_3_out14), .clk(clock), .Q(rqg14_q));  // open: clr
  Register #(.width(16)) reg15 (.D(writeData), .en(decoder_3_out15), .clk(clock), .Q(reg15_q));  // open: clr
  assign read_b = decoder_2_out7 ? reg7_q : 16'bz;  // Controlled_Buffer controlled_buffer_2
  assign read_b = decoder_2_out1 ? reg1_q : 16'bz;  // Controlled_Buffer controlled_buffer_3
  assign read_a = decoder_1_out8 ? reg8_q : 16'bz;  // Controlled_Buffer controlled_buffer_4
  assign read_b = decoder_2_out8 ? reg8_q : 16'bz;  // Controlled_Buffer controlled_buffer_5
  assign read_a = decoder_1_out1 ? reg1_q : 16'bz;  // Controlled_Buffer controlled_buffer_6
  assign read_a = decoder_1_out9 ? reg9_q : 16'bz;  // Controlled_Buffer controlled_buffer_7
  assign read_b = decoder_2_out9 ? reg9_q : 16'bz;  // Controlled_Buffer controlled_buffer_8
  assign read_a = decoder_1_out2 ? reg2_q : 16'bz;  // Controlled_Buffer controlled_buffer_9
  assign read_a = decoder_1_out10 ? reg10_q : 16'bz;  // Controlled_Buffer controlled_buffer_10
  assign read_b = decoder_2_out2 ? reg2_q : 16'bz;  // Controlled_Buffer controlled_buffer_11
  assign read_a = decoder_1_out3 ? reg3_q : 16'bz;  // Controlled_Buffer controlled_buffer_12
  assign read_a = decoder_1_out11 ? reg11_q : 16'bz;  // Controlled_Buffer controlled_buffer_13
  assign read_a = decoder_1_out4 ? reg4_q : 16'bz;  // Controlled_Buffer controlled_buffer_14
  assign read_a = decoder_1_out12 ? reg12_q : 16'bz;  // Controlled_Buffer controlled_buffer_15
  assign read_b = decoder_2_out12 ? reg12_q : 16'bz;  // Controlled_Buffer controlled_buffer_16
  assign read_a = decoder_1_out5 ? reg5_q : 16'bz;  // Controlled_Buffer controlled_buffer_17
  assign read_a = decoder_1_out13 ? reg13_q : 16'bz;  // Controlled_Buffer controlled_buffer_18
  assign read_a = decoder_1_out6 ? reg6_q : 16'bz;  // Controlled_Buffer controlled_buffer_19
  assign read_a = decoder_1_out14 ? rqg14_q : 16'bz;  // Controlled_Buffer controlled_buffer_20
  assign read_a = decoder_1_out7 ? reg7_q : 16'bz;  // Controlled_Buffer controlled_buffer_21
  assign read_a = decoder_1_out15 ? reg15_q : 16'bz;  // Controlled_Buffer controlled_buffer_22
  assign read_a = decoder_1_out0 ? reg0_q : 16'bz;  // Controlled_Buffer controlled_buffer_23
  assign read_b = decoder_2_out10 ? reg10_q : 16'bz;  // Controlled_Buffer controlled_buffer_24
  assign read_b = decoder_2_out13 ? reg13_q : 16'bz;  // Controlled_Buffer controlled_buffer_25
  assign read_b = decoder_2_out4 ? reg4_q : 16'bz;  // Controlled_Buffer controlled_buffer_26
  assign read_b = decoder_2_out15 ? reg15_q : 16'bz;  // Controlled_Buffer controlled_buffer_27
  assign read_b = decoder_2_out6 ? reg6_q : 16'bz;  // Controlled_Buffer controlled_buffer_28
  assign read_b = decoder_2_out11 ? reg11_q : 16'bz;  // Controlled_Buffer controlled_buffer_29
  assign read_b = decoder_2_out3 ? reg3_q : 16'bz;  // Controlled_Buffer controlled_buffer_30
  assign read_b = decoder_2_out14 ? rqg14_q : 16'bz;  // Controlled_Buffer controlled_buffer_31
  assign read_b = decoder_2_out5 ? reg5_q : 16'bz;  // Controlled_Buffer controlled_buffer_32
endmodule
